// Logisim project PROJETO-CONCEITO-COMPUTAÇAO-versãoCompleta66.circ as structural Verilog: 2 circuits, main circuit FUGICULTURA
module FUGICULTURA (
  input  P1_ABERTA,
  input  P2_ABERTA,
  input  H_ALTA,
  input  H_BAIXA,
  input  T_ALTA,
  input  T_BAIXO,
  input  L_ALTA,
  input  P_TX,
  output AQUECEDOR,
  output GOTEJADOR,
  output UMIDIFICADOR,
  output PARIEDADE_P,
  output ERRO_PARIEDADE,
  output LIBERAR_P1,
  output LIBERAR_P2,
  output VENTILADORES
);

  wire and_1_out, not_3_out, not_4_out, or_1_out, or_3_out, or_5_out;

  not not_1 (LIBERAR_P1, P1_ABERTA);
  not not_2 (LIBERAR_P2, P2_ABERTA);
  or or_1 (or_1_out, H_ALTA, T_ALTA);
  or or_2 (VENTILADORES, or_1_out, and_1_out);
  not not_3 (not_3_out, L_ALTA);
  or or_3 (or_3_out, T_ALTA, H_BAIXA);
  or or_4 (UMIDIFICADOR, H_BAIXA, T_BAIXO);
  and and_1 (and_1_out, P1_ABERTA, P2_ABERTA);
  LED CAMERA (.in(and_1_out));
  not not_4 (not_4_out, H_ALTA);
  and and_2 (AQUECEDOR, H_ALTA, not_3_out);
  and and_3 (GOTEJADOR, or_3_out, not_4_out);
  or or_5 (or_5_out, P1_ABERTA, P2_ABERTA);
  LED ALARME_PORTAS (.in(or_5_out));
  LED LAMPADAS (.in(not_3_out));
  PARIDADE paridade_1 (
    .H_ALTA(H_ALTA), .H_BAIXA(H_BAIXA), .T_ALTA(T_ALTA), .T_BAIXO(T_BAIXO), .L_ALTA(L_ALTA), .P_TX(P_TX),
    .ERRO_PARIDADE(ERRO_PARIEDADE), .PARIEDADE_P(PARIEDADE_P));
endmodule

module PARIDADE (
  input  H_ALTA,
  input  H_BAIXA,
  input  T_ALTA,
  input  T_BAIXO,
  input  L_ALTA,
  input  P_TX,
  output PARIEDADE_P,
  output ERRO_PARIDADE
);

  wire xor_1_out, xor_2_out, xor_3_out, xor_4_out;

  xor xor_1 (xor_1_out, T_BAIXO, H_BAIXA);
  xor xor_2 (xor_2_out, xor_1_out, H_ALTA);
  xor xor_3 (xor_3_out, xor_2_out, T_ALTA);
  not not_1 (PARIEDADE_P, xor_3_out);
  xor xor_4 (xor_4_out, xor_3_out, P_TX);
  not not_2 (ERRO_PARIDADE, xor_4_out);
endmodule
